# Fritzing sketch AudioPassController (saved by Fritzing 0.9.9b)
circuit board: 8.72152cm x 1.82276cm

parts:
  RL1 = DPDT Relay [chip_label=Relay package="DIP (Dual Inline) [THT]"]
  D1 = Rectifier Diode [part_number=1N007 package="300 mil [THT]"]
  Q1 = Basic FET P-Channel [part_number=TIP120 package="TO220 [THT]"]
  J1 = male pin header, 3 pins [form="♂ (male)"]
  R1 = Resistor [tolerance=±5% resistance=1k power=0.25 package="0603 [SMD]"]
  J3 = male pin header, 2 pins [form="♂ (male)"]
  J4 = male pin header, 2 pins [form="♂ (male)"]
  J2 = screw terminal, 4 pins
  C1 = Ceramic Capacitor [capacitance=1µF voltage=35V package="0805 [SMD, multilayer]"]
  R2 = Resistor [tolerance=±5% resistance=10k power=0.25 package="0603 [SMD]"]
  R3 = Resistor [tolerance=±5% resistance=10k power=0.25 package="0603 [SMD]"]

nets:
  N1: RL1.pin1, D1.anode, Q1.drain
  N2: RL1.pin2, J4.pin1
  N3: RL1.pin3, J2.pin3
  N4: RL1.pin4, R3.Pin_1
  N5: RL1.pin5, R2.Pin_1
  N6: RL1.pin6, J2.pin1
  N7: RL1.pin7, J3.pin1
  N8: RL1.pin8, D1.cathode, J1.pin2, C1.0
  N9: Q1.gate, R1.Pin_0
  N10: Q1.source, J1.pin3, C1.1
  N11: J1.pin1, R1.Pin_1
  N12: J3.pin2, J2.pin2, R2.Pin_0
  N13: J4.pin2, J2.pin4, R3.Pin_0

notes:
  AUDIO OFF
  GND
  5v
  pause or play command is active
  Relay to disable audio when
  Output
  Input
  L+ (White)
  L- (Blue)
  R+ (Red)
  R- (Green)
  L
  +  -
  R
  White
  Blue
  Red
  Green
  Audio Pass Controller Board v0.1 (Oct 2022)
  Automatic Record Player
  1
  +
  -
  COM
  _

custom parts:
  DPDT Relay: DIP DPDT Relay (Double Pole Double Throw)
