# Fritzing sketch AutoTurntable (saved by Fritzing 0.9.9b)
circuit board: 8cm x 17.4cm
breadboards: 3

parts:
  A1 = Arduino Nano (Rev3.0)
  J6 = shrouded pin header, 6 pins [form="♂ (shrouded male)"]
  J7 = shrouded pin header, 6 pins [form="♂ (shrouded male)"]
  J11 = shrouded pin header, 8 pins [form="♂ (shrouded male)"]
  U3 = ULN2003A [package="DIP16 [THT]"]
  U4 = ULN2003A [package="DIP16 [THT]"]
  J5 = male pin header, 4 pins [form="♂ (male)"]
  J14 = male pin header, 5 pins [form="♂ (male)"]
  J13 = male pin header, 5 pins [form="♂ (male)"]
  J24 = male pin header, 3 pins [form="♂ (male)"]
  J25 = male pin header, 3 pins [form="♂ (male)"]
  J26 = male pin header, 3 pins [form="♂ (male)"]
  J27 = shrouded pin header, 16 pins [form="♂ (shrouded male)"]
  D3 = Rectifier Diode [part_number=1N007 package="300 mil [THT]"]
  D4 = Rectifier Diode [part_number=1N007 package="300 mil [THT]"]
  D6 = Rectifier Diode [part_number=1N007 package="300 mil [THT]"]
  J1 = screw terminal, 2 pins
  Q2 = Basic FET P-Channel [part_number=TIP120 package="TO220 [THT]"]
  J8 = male pin header, 3 pins [form="♂ (male)"]
  J9 = male pin header, 3 pins [form="♂ (male)"]
  D9 = Rectifier Diode [part_number=1N007 package="300 mil [THT]"]
  D10 = Rectifier Diode [part_number=1N007 package="300 mil [THT]"]
  D7 = Rectifier Diode [part_number=1N007 package="300 mil [THT]"]
  D8 = Rectifier Diode [part_number=1N007 package="300 mil [THT]"]
  D5 = Rectifier Diode [part_number=1N007 package="300 mil [THT]"]
  R24 = Resistor [tolerance=±5% resistance=10k power=0.25 package="0603 [SMD]"]
  R10 = Resistor [tolerance=±5% resistance=10k power=0.25 package="0603 [SMD]"]
  R12 = Resistor [tolerance=±5% resistance=10k power=0.25 package="0603 [SMD]"]
  R11 = Resistor [tolerance=±5% resistance=10k power=0.25 package="0603 [SMD]"]
  R9 = Resistor [tolerance=±5% resistance=10k power=0.25 package="0603 [SMD]"]
  C6 = Ceramic Capacitor [capacitance="100 nF" voltage=35V package="0603 [SMD, multilayer]"]
  C3 = Ceramic Capacitor [capacitance="100 nF" voltage=35V package="0603 [SMD, multilayer]"]
  C4 = Ceramic Capacitor [capacitance="100 nF" voltage=35V package="0603 [SMD, multilayer]"]
  R15 = Resistor [tolerance=±5% resistance=10k power=0.25 package="0603 [SMD]"]
  R4 = Resistor [tolerance=±5% resistance=10k power=0.25 package="0603 [SMD]"]
  R5 = Resistor [tolerance=±5% resistance=10k power=0.25 package="0603 [SMD]"]
  R7 = Resistor [tolerance=±5% resistance=10k power=0.25 package="0603 [SMD]"]
  R13 = Resistor [tolerance=±5% resistance=10k power=0.25 package="0603 [SMD]"]
  R14 = Resistor [tolerance=±5% resistance=10k power=0.25 package="0603 [SMD]"]
  R23 = Resistor [tolerance=±5% resistance=1k power=0.25 package="0603 [SMD]"]
  U8 = 74AHC1G08 [package=sot23-5]
  C13 = Ceramic Capacitor [capacitance="100 nF" voltage=35V package="0603 [SMD, multilayer]"]
  R27 = Resistor [tolerance=±5% resistance=10k power=0.25 package="0603 [SMD]"]
  R26 = Resistor [tolerance=±5% resistance=10k power=0.25 package="0603 [SMD]"]
  C2 = Ceramic Capacitor [capacitance="100 nF" voltage=35V package="0603 [SMD, multilayer]"]
  J19 = male pin header, 2 pins [form="♂ (male)"]
  J20 = male pin header, 2 pins [form="♂ (male)"]
  J17 = male pin header, 2 pins [form="♂ (male)"]
  J18 = male pin header, 2 pins [form="♂ (male)"]
  J15 = male pin header, 2 pins [form="♂ (male)"]
  C7 = Ceramic Capacitor [capacitance=1µF voltage=35V package="0805 [SMD, multilayer]"]
  U9 = Voltage Regulator - Variable [package="TO220 [THT]"]
  C14 = Ceramic Capacitor [capacitance=10µF voltage=35V package="0805 [SMD, multilayer]"]
  R30 = Resistor [tolerance=±5% resistance=10k power=0.25 package="0603 [SMD]"]
  C15 = Ceramic Capacitor [capacitance="100 nF" voltage=35V package="0603 [SMD, multilayer]"]
  C16 = Ceramic Capacitor [capacitance="100 nF" voltage=35V package="0603 [SMD, multilayer]"]
  C17 = Ceramic Capacitor [capacitance="100 nF" voltage=35V package="0603 [SMD, multilayer]"]
  C18 = Ceramic Capacitor [capacitance="100 nF" voltage=35V package="0603 [SMD, multilayer]"]
  U10 = SN74LVC1G18DBVR [package=sot-23-6]
  U11 = SN74LVC1G18DBVR [package=sot-23-6]
  U12 = SN74LVC1G18DBVR [package=sot-23-6]
  U13 = SN74LVC1G18DBVR [package=sot-23-6]
  R32 = Resistor [tolerance=±5% resistance=10k power=0.25 package="0603 [SMD]"]
  D11 = Rectifier Diode [part_number=1N007 package="300 mil [THT]"]
  J28 = male pin header, 3 pins [form="♂ (male)"]
  J29 = male pin header, 3 pins [form="♂ (male)"]
  U1 = CD4051BE 8-channel mux [chip_label=IC package="DIP (Dual Inline) [THT]"]
  J30 = male pin header, 2 pins [form="♂ (male)"]
  U2 = MX1508 Motor Driver [chip_label=SOIC18-W package=SO]
  C22 = Capacitor Polarized [package=panasonic_d]
  R34 = Resistor [tolerance=±5% resistance=220 package="0805 [SMD]"]
  C23 = Capacitor Polarized [package=panasonic_d]
  RL1 = DPDT Relay [chip_label=Relay package="DIP (Dual Inline) [THT]"]
  J31 = male pin header, 2 pins [form="♂ (male)"]
  Q3 = Basic FET P-Channel [part_number=TIP120 package="TO220 [THT]"]
  R35 = Resistor [tolerance=±5% resistance=1k power=0.25 package="0603 [SMD]"]
  D13 = Rectifier Diode [part_number=1N007 package="300 mil [THT]"]
  J39 = male pin header, 1 pin [form="♂ (male)"]
  R36 = male pin header, 1 pin [form="♂ (male)"]
  D14 = Rectifier Diode [part_number=1N007 package="300 mil [THT]"]
  J33 = shrouded pin header, 6 pins [form="♂ (shrouded male)"]
  J34 = shrouded pin header, 6 pins [form="♂ (shrouded male)"]
  R37 = Resistor [tolerance=±5% resistance=10k power=0.25 package="0603 [SMD]"]
  J40 = male pin header, 1 pin [form="♂ (male)"]
  R38 = male pin header, 1 pin [form="♂ (male)"]
  J41 = male pin header, 1 pin [form="♂ (male)"]
  R39 = male pin header, 1 pin [form="♂ (male)"]
  U14 = Voltage Regulator - Variable [package="TO220 [THT]"]
  R40 = Resistor [tolerance=±5% resistance=10k power=0.25 package="0603 [SMD]"]
  C24 = Ceramic Capacitor [capacitance=10µF voltage=35V package="0805 [SMD, multilayer]"]
  J37 = screw terminal, 2 pins
  RL2 = DPDT Relay [chip_label=Relay package="DIP (Dual Inline) [THT]"]
  J38 = male pin header, 2 pins [form="♂ (male)"]
  D15 = Rectifier Diode [part_number=1N007 package="300 mil [THT]"]
  Q4 = Basic FET P-Channel [part_number=TIP120 package="TO220 [THT]"]
  R42 = Resistor [tolerance=±5% resistance=10k power=0.25 package="0603 [SMD]"]
  R41 = Resistor [tolerance=±5% power=0.25 resistance=10k package=THT]
  D12 = Diode [package=sma-diode-kit]
  RL3 = DPDT Relay [chip_label=Relay package="DIP (Dual Inline) [THT]"]
  D16 = Rectifier Diode [part_number=1N007 package="300 mil [THT]"]
  Q5 = Basic FET P-Channel [part_number=TIP120 package="TO220 [THT]"]
  R43 = Resistor [tolerance=±5% resistance=1k power=0.25 package="0603 [SMD]"]
  J42 = male pin header, 2 pins [form="♂ (male)"]
  J43 = male pin header, 2 pins [form="♂ (male)"]
  D17 = Rectifier Diode [part_number=1N007 package="300 mil [THT]"]
  D18 = Rectifier Diode [part_number=1N007 package="300 mil [THT]"]

nets:
  GND: A1.GND, U3.0V, U4.0V, J5.pin2, J24.pin3, J25.pin3, J26.pin3, J27.pin16, J1.pin2, Q2.source, R24.Pin_0, R10.Pin_1, R12.Pin_1, R11.Pin_1, R9.Pin_1, C6.1, C3.0, C4.1, R15.Pin_0, R4.Pin_1, R5.Pin_1, R7.Pin_1, R13.Pin_0, R14.Pin_0, U8.GND, C13.1, R27.Pin_0, R26.Pin_0, C2.1, C7.1, U9.GND, C14.1, R30.Pin_1, C15.0, C16.0, C17.1, C18.1, U10.GND, U11.GND, U12.GND, U13.GND, R32.Pin_1, J29.pin3, U1.Negative, U1.Ground, U2.idk_(connect_to_ground), C22.-, C23.-, Q3.source, J33.pin3, J34.pin3, U14.GND, R40.Pin_1, C24.1, Q4.source, R42.Pin_0, D12.A, Q5.source
  N1: A1.D2, U1.Selector_A
  N2: A1.D3, U1.Selector_B
  N3: A1.D4, U1.Selector_C
  N4: A1.D6, U1.COM_I/O
  N5: A1.D7, U13.A
  N6: A1.D8, U12.A
  N7: A1.D9, U11.A
  N8: A1.D10, U10.S, U11.S, U12.S, U13.S
  N9: A1.D11/MOSI, U10.A
  N10: A1.D12/MISO, U2.Motor_1_logic_1
  VDD: A1.VIN, J6.pin5, J7.pin2, J7.pin5, J11.pin1, U3.COM_-_Common, U4.COM_-_Common, J5.pin1, J14.pin1, J13.pin1, J24.pin2, J25.pin2, J26.pin2, J27.pin2, D6.anode, D5.anode, C6.0, C3.1, C4.0, U8.VCC, C13.0, C2.0, J17.pin1, J18.pin1, J15.pin2, C7.0, U9.OUT, C14.0, R30.Pin_0, C15.1, C16.1, C17.0, C18.0, U10.VDD, U11.VDD, U12.VDD, U13.VDD, J28.pin2, J29.pin2, U1.5v_input
  N11: A1.A7, J29.pin1
  N12: A1.A6, J25.pin1
  N13: A1.A5, J5.pin4
  N14: A1.A4, J5.pin3
  N15: A1.A3, J26.pin1
  N16: A1.A2, J24.pin1, J27.pin1, U8.A
  N17: A1.A1, U2.Motor_1_logic_2
  N18: A1.A0, J11.pin4, J27.pin5, D17.anode
  N19: A1.D13/SCK, J11.pin3, J27.pin6, D18.anode
  N20: J6.pin1, J6.pin3, J8.pin2, J9.pin2, U9.IN, U14.IN
  N21: J6.pin2, D11.cathode
  N22: J6.pin6, J27.pin14, R14.Pin_1, U1.Ch_5
  N23: J7.pin1, J7.pin3, J27.pin7, D7.anode
  N24: J7.pin6, D9.anode
  N25: J11.pin5, R4.Pin_0
  N26: J11.pin6, R5.Pin_0
  N27: J11.pin8, R7.Pin_0
  N28: U3.In_1, U10.Y1
  N29: U3.In_2, U11.Y1
  N30: U3.In_3, U12.Y1
  N31: U3.In_4, U13.Y1
  N32: U3.Out_4, J13.pin5
  N33: U3.Out_3, J13.pin4
  N34: U3.Out_2, J13.pin3
  N35: U3.Out_1, J13.pin2
  N36: U4.In_1, U10.Y0
  N37: U4.In_2, U11.Y0
  N38: U4.In_3, U12.Y0
  N39: U4.In_4, U13.Y0
  N40: U4.Out_4, J14.pin5
  N41: U4.Out_3, J14.pin4
  N42: U4.Out_2, J14.pin3
  N43: U4.Out_1, J14.pin2
  N44: J27.pin3, D3.anode
  N45: J27.pin4, D4.anode
  N46: J27.pin8, D10.anode
  N47: J27.pin9, D8.anode
  N48: J27.pin10, R15.Pin_1, J28.pin3, U1.Ch_7
  N49: J27.pin11, R13.Pin_1, J28.pin1, U1.Ch_4
  N50: D3.cathode, R10.Pin_0, J20.pin2, U1.Ch_1
  N51: D4.cathode, R11.Pin_0, J19.pin2, U1.Ch_2
  N52: D6.cathode, J20.pin1
  N53: J1.pin1, D11.anode
  N54: Q2.gate, R23.Pin_1, Q4.gate
  N55: Q2.drain, J31.pin2, D14.anode
  N56: J8.pin1, J39.pin1, J41.pin1
  N57: J8.pin3, R26.Pin_1
  N58: J9.pin1, J33.pin4, J40.pin1
  N59: J9.pin3, R27.Pin_1
  N60: D9.cathode, D10.cathode, R35.Pin_0
  N61: D7.cathode, D8.cathode, U8.B, R32.Pin_0
  N62: D5.cathode, J19.pin1
  N63: R24.Pin_1, J15.pin1, U1.Ch_6
  N64: R12.Pin_0, J18.pin2, U1.Ch_3
  N65: R9.Pin_0, J17.pin2, U1.Ch_0
  N66: R23.Pin_0, U8.Y
  N67: U1.Disable_channels, R42.Pin_1
  N68: J30.pin1, U2.Motor_1_out_2
  N69: J30.pin2, U2.Motor_1_out_1
  N70: U2.VCC1, U2.VCC2, R34.Pin_1, C23.+, D12.C
  N71: U2.+5v_(VDD2_-_use_this_one), C22.+, R34.Pin_0, RL1.pin8, D13.cathode, R37.Pin_1, U14.OUT, R40.Pin_0, C24.0, RL2.pin8, D15.cathode, RL3.pin8, D16.cathode
  N72: RL1.pin1, Q3.drain, D13.anode
  N73: RL1.pin5, J34.pin5
  N74: RL1.pin6, J33.pin5
  N75: RL1.pin7, J31.pin1, D14.cathode
  N76: Q3.gate, R35.Pin_1
  N77: R36.pin1, J34.pin6
  N78: J33.pin2, J34.pin2, R37.Pin_0
  N79: J33.pin6, R38.pin1
  N80: J34.pin4, R39.pin1
  N81: J37.pin1, RL2.pin7
  N82: J37.pin2, J38.pin1
  N83: RL2.pin1, D15.anode, Q4.drain
  N84: RL2.pin5, R41.Pin_1
  N85: J38.pin2, R41.Pin_0
  N86: RL3.pin1, D16.anode, Q5.drain
  N87: RL3.pin2, J42.pin2
  N88: RL3.pin3, J43.pin2
  N89: RL3.pin6, J43.pin1
  N90: RL3.pin7, J42.pin1
  N91: Q5.gate, R43.Pin_1
  N92: R43.Pin_0, D17.cathode, D18.cathode

notes:
  Power SW
  Speed SW
  Size SW
  LEDs
  PW SW
  SZ SW
  7-Seg Disp.
  7S DISP
  Vertical Motor
  Horiz. Motor
  [
  Upper Limit
  Lower Limit
  V MTR
  H MTR
  Pause Button
  Play/Home Button
  U LIM
  L LIM
  PA BT
  PL BT
  Home Sensor
  HOME
  Pickup Sensor
  Speed Sensor
  SPEED
  PICKUP
  33-RPM Pot
  45-RPM Pot
  33 POT
  45 POT
  TURN MTR
  SPD SW
  Automatic Changer Comm
  _
  GND
  +5v
  5v DC
  3.3v DC
  Mux S16
  Mux S15
  Auto-mode indicator (Mux S12)
  5v DC in
  5v DC out
  NC
  Turntable power indicator LED
  33-RPM pot
  J12 pin 2
  45-RPM pot
  J12 pin 3
  J12 pin 4
  Q3 drain
  J10 pin 5
  Power indicator LED (5v)
  Turntable power indicator LED (J10 pin 3)
  Pause status LED (Ard. D13)
  Play status LED (Ard. D12)
  Play status LED GND
  Pause status LED GND
  Turntable power indicator LED GND
  Power indicator LED GND
  SW 1
  SW 2
  SW 3
  SW 4
  SW 5
  SW 6
  1
  Automatic Record Player v0.4 (September 2022)
  Designed by Patrick Nelson (github.com/pdnelson)
  Calibration Display Button
  CAL
  12v DC in
  12v DC
  -
  +
  Main 5v circuit
  ]
  Pickup Sensor Direction
  Horizontal Engagement Motor Controller
  Horizontal Engagement Motor
  Turn Motor
  33 RPM resistor
  78 speed button
  16 2/3 speed button
  45 RPM resistor
  16 RPM resistor
  6.3v AC in
  Strobe LEDs
  HG MTR
  16 SW
  78 SW
  PICKUP D
  16
  Audio in
  Audio out
  Relay to disable audio when
  pause or play command is active
  L-R O
  L-R I

custom parts:
  Voltage Regulator - Variable: Variable DC Voltage Regulator
  CD4051BE 8-channel mux: A DIP stand-in part for whatever IC you want. With 16 pins on a 300mil dual inline package (DIP) footprint.
  DPDT Relay: DIP DPDT Relay (Double Pole Double Throw)
