# Fritzing sketch TurntableMain (saved by Fritzing 0.9.9b)
circuit board: 8cm x 8cm
breadboards: 3

parts:
  A1 = Arduino Nano (Rev3.0)
  J3 = shrouded pin header, 6 pins [form="♂ (shrouded male)"]
  J4 = shrouded pin header, 6 pins [form="♂ (shrouded male)"]
  J21 = shrouded pin header, 8 pins [form="♂ (shrouded male)"]
  U3 = ULN2003A [package="DIP16 [THT]"]
  U2 = ULN2003A [package="DIP16 [THT]"]
  J7 = male pin header, 5 pins [form="♂ (male)"]
  J8 = male pin header, 5 pins [form="♂ (male)"]
  J18 = male pin header, 3 pins [form="♂ (male)"]
  J19 = male pin header, 3 pins [form="♂ (male)"]
  J12 = shrouded pin header, 16 pins [form="♂ (shrouded male)"]
  J1 = screw terminal, 2 pins
  R9 = Resistor [tolerance=±5% resistance=10k power=0.25 package="0603 [SMD]"]
  R11 = Resistor [tolerance=±5% resistance=10k power=0.25 package="0603 [SMD]"]
  R8 = Resistor [tolerance=±5% resistance=10k power=0.25 package="0603 [SMD]"]
  R10 = Resistor [tolerance=±5% resistance=10k power=0.25 package="0603 [SMD]"]
  C5 = Ceramic Capacitor [capacitance="100 nF" voltage=35V package="0603 [SMD, multilayer]"]
  C19 = Ceramic Capacitor [capacitance="100 nF" voltage=35V package="0603 [SMD, multilayer]"]
  R14 = Resistor [tolerance=±5% resistance=10k power=0.25 package="0603 [SMD]"]
  R4 = Resistor [tolerance=±5% resistance=10k power=0.25 package="0603 [SMD]"]
  R5 = Resistor [tolerance=±5% resistance=1k power=0.25 package="0603 [SMD]"]
  R7 = Resistor [tolerance=±5% resistance=1k power=0.25 package="0603 [SMD]"]
  R16 = Resistor [tolerance=±5% resistance=10k power=0.25 package="0603 [SMD]"]
  R13 = Resistor [tolerance=±5% resistance=10k power=0.25 package="0603 [SMD]"]
  U9 = 74AHC1G08 [package=sot23-5]
  C8 = Ceramic Capacitor [capacitance="100 nF" voltage=35V package="0603 [SMD, multilayer]"]
  J10 = male pin header, 2 pins [form="♂ (male)"]
  J11 = male pin header, 2 pins [form="♂ (male)"]
  J15 = male pin header, 2 pins [form="♂ (male)"]
  J14 = male pin header, 2 pins [form="♂ (male)"]
  C20 = Ceramic Capacitor [capacitance=1µF voltage=35V package="0805 [SMD, multilayer]"]
  U6 = Voltage Regulator - Variable [package="TO220 [THT]"]
  C11 = Ceramic Capacitor [capacitance=10µF voltage=35V package="0805 [SMD, multilayer]"]
  R3 = Resistor [tolerance=±5% resistance=10k power=0.25 package="0603 [SMD]"]
  C24 = Ceramic Capacitor [capacitance="100 nF" voltage=35V package="0603 [SMD, multilayer]"]
  C23 = Ceramic Capacitor [capacitance="100 nF" voltage=35V package="0603 [SMD, multilayer]"]
  C22 = Ceramic Capacitor [capacitance="100 nF" voltage=35V package="0603 [SMD, multilayer]"]
  C21 = Ceramic Capacitor [capacitance="100 nF" voltage=35V package="0603 [SMD, multilayer]"]
  U15 = SN74LVC1G18DBVR [package=sot-23-6]
  U16 = SN74LVC1G18DBVR [package=sot-23-6]
  U17 = SN74LVC1G18DBVR [package=sot-23-6]
  U18 = SN74LVC1G18DBVR [package=sot-23-6]
  U5 = CD4051BE 8-channel mux [chip_label=IC package="DIP (Dual Inline) [THT]"]
  J9 = male pin header, 2 pins [form="♂ (male)"]
  U4 = MX1508 Motor Driver [chip_label=SOIC18-W package=SO]
  C2 = Capacitor Polarized [package=panasonic_d]
  R1 = Resistor [tolerance=±5% resistance=220 package="0805 [SMD]"]
  C3 = Capacitor Polarized [package=panasonic_d]
  U1 = Voltage Regulator - Variable [package="TO220 [THT]"]
  R2 = Resistor [tolerance=±5% resistance=10k power=0.25 package="0603 [SMD]"]
  C4 = Ceramic Capacitor [capacitance=10µF voltage=35V package="0805 [SMD, multilayer]"]
  R12 = Resistor [tolerance=±5% resistance=10k power=0.25 package="0603 [SMD]"]
  D1 = Diode [package=sma-diode-kit]
  J5 = male pin header, 2 pins [form="♂ (male)"]
  J16 = male pin header, 3 pins [form="♂ (male)"]
  J6 = male pin header, 5 pins [form="♂ (male)"]
  J20 = male pin header, 4 pins [form="♂ (male)"]
  R15 = Resistor [tolerance=±5% resistance=10k power=0.25 package="0603 [SMD]"]
  C10 = Ceramic Capacitor [capacitance="100 nF" voltage=35V package="0603 [SMD, multilayer]"]
  C9 = Ceramic Capacitor [capacitance="100 nF" voltage=35V package="0603 [SMD, multilayer]"]
  C12 = Ceramic Capacitor [capacitance="100 nF" voltage=35V package="0603 [SMD, multilayer]"]
  C14 = Ceramic Capacitor [capacitance="100 nF" voltage=35V package="0603 [SMD, multilayer]"]
  C13 = Ceramic Capacitor [capacitance="100 nF" voltage=35V package="0603 [SMD, multilayer]"]
  D2 = Diode [package=sma-diode]
  C6 = Ceramic Capacitor [capacitance="100 nF" voltage=35V package="0603 [SMD, multilayer]"]
  C17 = Ceramic Capacitor [capacitance="100 nF" voltage=35V package="0603 [SMD, multilayer]"]
  C15 = Ceramic Capacitor [capacitance="100 nF" voltage=35V package="0603 [SMD, multilayer]"]
  C16 = Ceramic Capacitor [capacitance=47nF voltage=35V package="0603 [SMD, multilayer]"]
  C18 = Ceramic Capacitor [capacitance=47nF voltage=35V package="0603 [SMD, multilayer]"]
  U14 = MC74VHC1G32DTT1G [package=sot23-5]
  U10 = MC74VHC1G32DTT1G [package=sot23-5]
  U13 = MC74VHC1G32DTT1G [package=sot23-5]
  U7 = MC74VHC1G32DTT1G [package=sot23-5]
  U11 = MC74VHC1G32DTT1G [package=sot23-5]
  U12 = MC74VHC1G32DTT1G [package=sot23-5]
  C1 = Ceramic Capacitor [capacitance="100 nF" voltage=35V package="0603 [SMD, multilayer]"]
  U8 = 74AHC1G08 [package=sot23-5]
  C7 = Ceramic Capacitor [capacitance="100 nF" voltage=35V package="0603 [SMD, multilayer]"]
  J13 = male pin header, 2 pins [form="♂ (male)"]
  R6 = Resistor [tolerance=±5% resistance=1k power=0.25 package="0603 [SMD]"]
  J17 = male pin header, 2 pins [form="♂ (male)"]
  J2 = male pin header, 1 pin [form="♂ (male)"]

nets:
  GND: A1.GND, U3.0V, U2.0V, J18.pin3, J19.pin3, J12.pin4, J1.pin2, R9.Pin_1, R11.Pin_1, R8.Pin_1, R10.Pin_1, C5.0, C19.1, R14.Pin_0, R4.Pin_1, R5.Pin_1, R7.Pin_1, R16.Pin_0, R13.Pin_0, U9.GND, C8.1, C20.1, U6.GND, C11.1, R3.Pin_1, C24.0, C23.0, C22.1, C21.1, U15.GND, U16.GND, U17.GND, U18.GND, U5.Negative, U5.Ground, U4.idk_(connect_to_ground), C2.-, C3.-, U1.GND, R2.Pin_1, C4.1, R12.Pin_0, D1.A, J16.pin3, J6.pin4, J20.pin4, R15.Pin_0, C10.0, C9.0, C12.0, C14.1, C13.1, C6.1, C17.0, C15.0, C16.0, C18.0, U14.GND, U10.GND, U13.GND, U7.GND, U11.GND, U12.GND, C1.1, U8.GND, C7.1, R6.Pin_1
  N1: A1.D2, U15.S, U16.S, U17.S, U18.S
  N2: A1.D3, U18.A
  N3: A1.D4, U17.A
  N4: A1.D5, U16.A
  N5: A1.D6, U15.A
  N6: A1.D7, U5.Selector_C
  N7: A1.D8, U5.Selector_B
  N8: A1.D9, U5.Selector_A
  N9: A1.D10, U5.COM_I/O
  N10: A1.D11/MOSI, U4.Motor_1_logic_1
  N11: A1.D12/MISO, U4.Motor_1_logic_2
  VCC: A1.VIN, J3.pin5, J4.pin2, J4.pin5, J21.pin1, J18.pin2, J19.pin2, J12.pin15, U9.VCC, C8.0, J10.pin1, J11.pin1, J15.pin1, J14.pin1, C20.0, U6.OUT, C11.0, R3.Pin_0, C24.1, C23.1, C22.0, C21.0, U15.VDD, U16.VDD, U17.VDD, U18.VDD, U5.5v_input, J5.pin2, J16.pin2, J20.pin2, C10.1, C9.1, C12.1, C14.0, C13.0, C6.0, U14.VCC, U10.VCC, U13.VCC, U7.VCC, U11.VCC, U12.VCC, C1.0, U8.VCC, C7.0, J13.pin1, J17.pin1
  N12: A1.A7, J21.pin3, J12.pin13, U12.B
  N13: A1.A6, J21.pin4, J12.pin14, U12.A
  N14: A1.A5, J20.pin3
  N15: A1.A4, J20.pin1
  N16: A1.A3, J19.pin1
  N17: A1.A2, J18.pin1, J12.pin16, U9.A
  N18: A1.A1, J21.pin2, J12.pin3, J17.pin2
  N19: A1.A0, J2.pin1
  N20: A1.D13/SCK, U8.B
  N21: J3.pin1, J3.pin3, U6.IN, U1.IN, J6.pin5
  N22: J3.pin2, D2.C
  N23: J3.pin6, J12.pin6, R14.Pin_1, U5.Ch_7
  N24: J4.pin1, J4.pin3, J12.pin5, U7.B
  N25: J4.pin6, U11.A
  N26: J21.pin5, R4.Pin_0
  N27: J21.pin6, R5.Pin_0
  N28: J21.pin7, R6.Pin_0
  N29: J21.pin8, R7.Pin_0
  N30: U3.In_1, U15.Y1
  N31: U3.In_2, U16.Y1
  N32: U3.In_3, U17.Y1
  N33: U3.In_4, U18.Y1
  N34: U3.COM_-_Common, U2.COM_-_Common, J7.pin1, J8.pin1, C5.1, C19.0, U4.+5v_(VDD2_-_use_this_one), C2.+, R1.Pin_0, U1.OUT, R2.Pin_0, C4.0, C17.1, C15.1, C16.1, C18.1
  N35: U3.Out_4, J8.pin5
  N36: U3.Out_3, J8.pin4
  N37: U3.Out_2, J8.pin3
  N38: U3.Out_1, J8.pin2
  N39: U2.In_1, U15.Y0
  N40: U2.In_2, U16.Y0
  N41: U2.In_3, U17.Y0
  N42: U2.In_4, U18.Y0
  N43: U2.Out_4, J7.pin5
  N44: U2.Out_3, J7.pin4
  N45: U2.Out_2, J7.pin3
  N46: U2.Out_1, J7.pin2
  N47: J12.pin7, U14.B
  N48: J12.pin8, U13.B
  N49: J12.pin9, U7.A
  N50: J12.pin10, U10.A
  N51: J12.pin11, J5.pin1, U10.B
  N52: J12.pin12, U11.B
  N53: J1.pin1, D2.A
  N54: R9.Pin_0, U5.Ch_1, U14.Y
  N55: R11.Pin_0, U5.Ch_3, J6.pin2, U10.Y
  N56: R8.Pin_0, U5.Ch_2, U13.Y
  N57: R10.Pin_0, U5.Ch_0, J6.pin1, U11.Y
  N58: R16.Pin_1, U5.Ch_4, J13.pin2
  N59: R13.Pin_1, J15.pin2, U5.Ch_5
  N60: U9.B, U8.Y
  N61: U9.Y, J6.pin3
  N62: J10.pin2, U14.A
  N63: J11.pin2, U13.A
  N64: J14.pin2, U5.Ch_6, R15.Pin_1
  N65: U5.Disable_channels, R12.Pin_1
  N66: J9.pin1, U4.Motor_1_out_2
  N67: J9.pin2, U4.Motor_1_out_1
  N68: U4.VCC1, U4.VCC2, R1.Pin_1, C3.+, D1.C
  N69: J16.pin1, U12.Y
  N70: U7.Y, U8.A

notes:
  Power SW
  Speed SW
  LEDs
  PW SW
  Vertical Motor
  Horiz. Motor
  [
  Upper Limit
  Lower Limit
  V MTR
  H MTR
  Pause Button
  Play/Home Button
  U LIM
  L LIM
  PA BT
  PL BT
  Home Sensor
  HOME
  Pickup Encoder
  Speed Sensor
  SPD.
  ENC.
  SPD SW
  Automatic Changer Comm
  GND
  +5v
  5v DC
  3.3v DC
  Mux S16
  Mux S15
  Auto-mode indicator (Mux S12)
  5v DC in
  5v DC out
  NC
  Turntable power indicator LED
  33-RPM pot
  J12 pin 2
  45-RPM pot
  J12 pin 3
  J12 pin 4
  Q3 drain
  J10 pin 5
  Power indicator LED (5v)
  Turntable power indicator LED (J10 pin 3)
  Pause status LED (Ard. D13)
  Play status LED (Ard. D12)
  Play status LED GND
  Pause status LED GND
  Turntable power indicator LED GND
  Power indicator LED GND
  SW 1
  SW 2
  SW 3
  SW 4
  SW 5
  SW 6
  _
  Automatic Record Player v0.5 (Dec. 2022)
  Patrick N. (github.com/pdnelson)
  12v DC in
  12v DC
  -
  +
  Main 5v circuit
  ]
  Horizontal Engagement Motor Controller
  Horizontal Engagement Motor
  CLTC
  Alt. Speed Button
  SPD 2
  AUD.
  TRN MTR
  Turn Motor Comm
  Motor 5v Circuit
  Wait Until Target Speed
  WAIT
  Repeat
  RPT
  Lift Indicator
  LIFT

custom parts:
  Voltage Regulator - Variable: Variable DC Voltage Regulator
  CD4051BE 8-channel mux: A DIP stand-in part for whatever IC you want. With 16 pins on a 300mil dual inline package (DIP) footprint.
  MC74VHC1G32DTT1G: Single 2-input OR gate
