# Fritzing sketch TurntableMotorController (saved by Fritzing 0.9.9b)
circuit board: 8.34252cm x 4.48246cm

parts:
  J10 = male pin header, 5 pins [form="♂ (male)"]
  RL1 = DPDT Relay [chip_label=Relay package="DIP (Dual Inline) [THT]"]
  Q1 = Basic FET P-Channel [part_number=TIP120 package="TO220 [THT]"]
  U1 = Voltage Regulator - Variable [package="TO220 [THT]"]
  D1 = Rectifier Diode [part_number=1N007 package="300 mil [THT]"]
  RL2 = DPDT Relay [chip_label=Relay package="DIP (Dual Inline) [THT]"]
  D2 = Rectifier Diode [part_number=1N007 package="300 mil [THT]"]
  RL3 = DPDT Relay [chip_label=Relay package="DIP (Dual Inline) [THT]"]
  D3 = Rectifier Diode [part_number=1N007 package="300 mil [THT]"]
  Q2 = Basic FET P-Channel [part_number=TIP120 package="TO220 [THT]"]
  Q3 = Basic FET P-Channel [part_number=TIP120 package="TO220 [THT]"]
  J4 = male pin header, 1 pin [form="♂ (male)"]
  J4_2 = male pin header, 1 pin [form="♂ (male)"]
  J4_3 = male pin header, 1 pin [form="♂ (male)"]
  J4_4 = male pin header, 1 pin [form="♂ (male)"]
  J1 = male pin header, 1 pin [form="♂ (male)"]
  J1_2 = male pin header, 1 pin [form="♂ (male)"]
  J1_3 = male pin header, 1 pin [form="♂ (male)"]
  J1_4 = male pin header, 1 pin [form="♂ (male)"]
  J3 = male pin header, 1 pin [form="♂ (male)"]
  J3_2 = male pin header, 1 pin [form="♂ (male)"]
  J3_3 = male pin header, 1 pin [form="♂ (male)"]
  J3_4 = male pin header, 1 pin [form="♂ (male)"]
  J5 = male pin header, 1 pin [form="♂ (male)"]
  J6 = male pin header, 1 pin [form="♂ (male)"]
  J7 = male pin header, 1 pin [form="♂ (male)"]
  J8 = male pin header, 1 pin [form="♂ (male)"]
  J9 = male pin header, 1 pin [form="♂ (male)"]
  R7 = male pin header, 1 pin [form="♂ (male)"]
  R7_2 = male pin header, 1 pin [form="♂ (male)"]
  R6 = male pin header, 1 pin [form="♂ (male)"]
  R6_2 = male pin header, 1 pin [form="♂ (male)"]
  R5 = male pin header, 1 pin [form="♂ (male)"]
  R5_2 = male pin header, 1 pin [form="♂ (male)"]
  J2 = male pin header, 1 pin [form="♂ (male)"]
  J2_2 = male pin header, 1 pin [form="♂ (male)"]
  J2_3 = male pin header, 1 pin [form="♂ (male)"]
  J2_4 = male pin header, 1 pin [form="♂ (male)"]
  C1 = Ceramic Capacitor [capacitance=10µF voltage=35V package="0805 [SMD, multilayer]"]
  R1 = Resistor [tolerance=±5% resistance=1k power=0.25 package="0603 [SMD]"]
  R2 = Resistor [tolerance=±5% resistance=1k power=0.25 package="0603 [SMD]"]
  R4 = Resistor [tolerance=±5% resistance=10k power=0.25 package="0603 [SMD]"]
  R3 = Resistor [tolerance=±5% resistance=1k power=0.25 package="0603 [SMD]"]
  C2 = Ceramic Capacitor [capacitance=1µF voltage=16V package="0805 [SMD, multilayer]"]
  C3 = Ceramic Capacitor [capacitance=1µF voltage=16V package="0805 [SMD, multilayer]"]
  C4 = Ceramic Capacitor [capacitance=1µF voltage=16V package="0805 [SMD, multilayer]"]

nets:
  N1: J10.pin1, R3.Pin_1
  N2: J10.pin2, R2.Pin_1
  N3: J10.pin3, R1.Pin_1
  N4: J10.pin4, Q1.source, U1.GND, Q2.source, Q3.source, C1.1, R4.Pin_1, C2.1, C3.1, C4.1
  N5: J10.pin5, U1.IN
  N6: RL1.pin1, Q1.drain, D1.anode
  N7: RL1.pin2, J1.pin1, J1_2.pin1, J1_3.pin1, J1_4.pin1
  N8: RL1.pin4, RL2.pin2
  N9: RL1.pin8, U1.OUT, D1.cathode, RL2.pin8, D2.cathode, RL3.pin8, D3.cathode, C1.0, R4.Pin_0, C2.0, C3.0, C4.0
  N10: Q1.gate, R1.Pin_0
  N11: RL2.pin1, D2.anode, Q2.drain
  N12: RL2.pin3, RL3.pin2
  N13: RL2.pin4, RL3.pin7
  N14: RL3.pin1, D3.anode, Q3.drain
  N15: RL3.pin3, R7.pin1
  N16: RL3.pin4, J9.pin1
  N17: RL3.pin5, R5.pin1
  N18: RL3.pin6, R6.pin1
  N19: Q2.gate, R2.Pin_0
  N20: Q3.gate, R3.Pin_0
  N21: J4.pin1, J4_2.pin1, J4_3.pin1, J4_4.pin1, J5.pin1
  N22: J3.pin1, J3_2.pin1, J3_3.pin1, J3_4.pin1, J2.pin1, J2_2.pin1, J2_3.pin1, J2_4.pin1
  N23: J6.pin1, R5_2.pin1
  N24: J7.pin1, R6_2.pin1
  N25: J8.pin1, R7_2.pin1

notes:
  12v
  GND
  TT ON
  SPD SEL A
  SPD SEL B
  Turntable Power
  Speed Selector A
  Speed Selector B
  MTR -
  MTR +
  12v Out Pot
  16 pot in
  33 pot in
  45 pot in
  78 pot in
  45 res
  33 res
  16 res
  12v in
  Automatic Record Player
  Motor Controller Board v0.1 (Oct 2022)
  _
  16
  33
  45
  78
  COM
  1

custom parts:
  DPDT Relay: DIP DPDT Relay (Double Pole Double Throw)
  Voltage Regulator - Variable: Variable DC Voltage Regulator
